# Fritzing sketch IP35D (saved by Fritzing 0.9.3b)
breadboards: 1

parts:
  Composant1 = Arduino Uno (Rev3)
  RGB_SMD_LED4 = SMD RGB LED (WS2812) [package=5050]
  Composant2 = Bluetooth HC-05 Macho
  RGB_SMD_LED5 = SMD RGB LED (WS2812) [package=5050]
  RGB_SMD_LED6 = SMD RGB LED (WS2812) [package=5050]
  e-radionica1 = TCS230 Color Sensor [part_number=101209]

nets:
  N1: Composant1.D12/MISO, RGB_SMD_LED4.DIn
  N2: Composant1.D13/SCK, e-radionica1.OE
  GND: Composant1.GND, RGB_SMD_LED4.VSS, Composant2.GND, e-radionica1.Gnd
  N3: Composant1.D0/RX, Composant2.TXD
  N4: Composant1.D1/TX, Composant2.RXD
  N5: Composant1.D2, e-radionica1.Out
  N6: Composant1.D3_PWM, e-radionica1.S3
  N7: Composant1.D4, e-radionica1.S2
  N8: Composant1.D5_PWM, e-radionica1.S1
  N9: Composant1.D6_PWM, e-radionica1.S0
  VCC: Composant1.5V, RGB_SMD_LED4.VCC, Composant2.VCC, e-radionica1.Vcc
  N10: RGB_SMD_LED4.DOut, RGB_SMD_LED5.DIn
  VDD: RGB_SMD_LED4.VDD, RGB_SMD_LED5.VCC
  N11: RGB_SMD_LED5.DOut, RGB_SMD_LED6.DIn
  VDD_2: RGB_SMD_LED5.VDD, RGB_SMD_LED6.VCC

custom parts:
  TCS230 Color Sensor: TCS230
